// Logisim project BAT8clean.circ as structural Verilog: 4 circuits, main circuit main
module main (
);

  wire A_R, A_W, and_1_out, and_2_out, and_3_out, and_4_out, B_R, B_W, C, C_C, clock_1_out,
       controlled_inverter_1_out, controlled_inverter_2_out, I_R, I_W, L_R, L_W, not_1_out, not_2_out,
       not_3_out, not_4_out, not_5_out, O, or_1_out, or_3_out, P, P_R, pull_resistor_1_node, R_a, R_R, R_W,
       RST_out, STATE_q0, STATE_q1, STATE_q2, STATE_q3, STATE_q4, T_R, T_W, TS1, TS2, TS3, TS4, TS5, Z, Z_C;
  wire [1:0] controlled_buffer_8_out;
  wire [7:0] ALU_res, controlled_buffer_1_out, controlled_buffer_5_out, counter_1_q, INS, OUT_out,
       rom_1_data, T_out;
  wire [15:0] rom_2_data;

  assign controlled_inverter_1_out = O ? ~Z : 1'bz;  // Controlled_Inverter controlled_inverter_1
  assign controlled_inverter_2_out = O ? ~C : 1'bz;  // Controlled_Inverter controlled_inverter_2
  assign controlled_buffer_1_out = R_a ? T_out : 8'bz;  // Controlled_Buffer controlled_buffer_1
  assign controlled_buffer_1_out = not_3_out ? counter_1_q : 8'bz;  // Controlled_Buffer controlled_buffer_2
  not not_1 (not_1_out, O);
  assign controlled_inverter_1_out = not_1_out ? Z : 1'bz;  // Controlled_Buffer controlled_buffer_3
  not not_2 (not_2_out, O);
  assign controlled_inverter_2_out = not_2_out ? C : 1'bz;  // Controlled_Buffer controlled_buffer_4
  ALU ALU (
    .RES(ALU_res), .CARRY(Z), .ZERO(C), .CLOCK(clock_1_out), .WRITE(L_W), .READ(L_R), .OP(O), .IN1(ALU_res),
    .IN2(T_out));
  and and_1 (and_1_out, C_C, controlled_inverter_1_out);
  and and_2 (and_2_out, controlled_inverter_2_out, Z_C);
  or or_1 (or_1_out, and_1_out, P_R, and_2_out);
  not not_3 (not_3_out, R_a);
  and and_3 (and_3_out, controlled_buffer_1_out[7], ~controlled_buffer_1_out[6]);  // AND_Gate
  not not_4 (not_4_out, controlled_buffer_1_out[7]);
  not not_5 (not_5_out, R_R);
  reg8 IR (.RST(RST_out), .OUT(INS), .CLOCK(clock_1_out), .WRITE(I_W), .READ(I_R), .IN(ALU_res));
  reg8 B (.RST(RST_out), .OUT(ALU_res), .CLOCK(clock_1_out), .WRITE(B_W), .READ(B_R), .IN(ALU_res));
  Counter counter_1 (
    .load(or_1_out), .D(T_out), .count(P), .Q(counter_1_q), .clk(clock_1_out), .clr(RST_out));  // open: carry
  and and_4 (and_4_out, ~controlled_buffer_1_out[0], ~controlled_buffer_1_out[1], ~controlled_buffer_1_out[2], ~controlled_buffer_1_out[3], ~controlled_buffer_1_out[4], ~controlled_buffer_1_out[5], controlled_buffer_1_out[7], controlled_buffer_1_out[6]);  // AND_Gate
  ROM #(.addrWidth(7)) rom_1 (.addr(controlled_buffer_1_out[6:0]), .data(rom_1_data), .sel(not_4_out));
  assign controlled_buffer_5_out = R_W ? rom_1_data : 8'bz;  // Controlled_Buffer controlled_buffer_5
  RAM #(.addrWidth(6)) ram_1 (
    .addr(controlled_buffer_1_out[5:0]), .data(controlled_buffer_5_out), .sel(and_3_out), .clk(clock_1_out),
    .ld(not_5_out), .clr(RST_out));
  // Probe on ALU_res
  reg8 A (.RST(RST_out), .OUT(ALU_res), .CLOCK(clock_1_out), .WRITE(A_W), .READ(A_R), .IN(ALU_res));
  reg8 OUT (
    .RST(RST_out), .OUT(OUT_out), .CLOCK(clock_1_out), .WRITE(1'b1), .READ(and_4_out),
    .IN(controlled_buffer_5_out));
  assign controlled_buffer_5_out = R_R ? ALU_res : 8'bz;  // Controlled_Buffer controlled_buffer_6
  assign ALU_res = R_W ? controlled_buffer_5_out : 8'bz;  // Controlled_Buffer controlled_buffer_7
  reg8 T (.RST(RST_out), .OUT(T_out), .CLOCK(clock_1_out), .WRITE(T_W), .READ(T_R), .IN(ALU_res));
  Button RST (.out(RST_out));
  Clock clock_1 (.out(clock_1_out));
  Hex_Digit_Display hex_digit_display_1 (.value(OUT_out[3:0]));  // open: dp
  Hex_Digit_Display hex_digit_display_2 (.value(OUT_out[7:4]));  // open: dp
  Shift_Register #(.length(5), .trigger("falling")) STATE (
    .in(STATE_q4), .clk(clock_1_out), .load(RST_out), .d0(1'b1), .q0(STATE_q0), .d1(1'b0), .q1(STATE_q1),
    .d2(1'b0), .q2(STATE_q2), .d3(1'b0), .q3(STATE_q3), .d4(1'b0), .q4(STATE_q4));  // open: shift, out, clr
  buf buffer_1 (TS1, STATE_q1);
  buf buffer_2 (TS3, STATE_q3);
  buf buffer_3 (TS2, STATE_q2);
  buf buffer_4 (I_R, STATE_q0);
  assign controlled_buffer_8_out = TS2 ? 2'b00 : 2'bz;  // Controlled_Buffer controlled_buffer_8
  assign controlled_buffer_8_out = TS3 ? 2'b01 : 2'bz;  // Controlled_Buffer controlled_buffer_9
  assign controlled_buffer_8_out = TS4 ? 2'b10 : 2'bz;  // Controlled_Buffer controlled_buffer_10
  assign controlled_buffer_8_out = TS5 ? 2'b11 : 2'bz;  // Controlled_Buffer controlled_buffer_11
  buf buffer_5 (TS5, pull_resistor_1_node);
  Pull_Resistor pull_resistor_1 (.node(pull_resistor_1_node));
  buf buffer_6 (TS4, STATE_q4);
  or or_2 (I_W, TS2, TS3, TS4);
  ROM #(.dataWidth(16)) rom_2 (.addr({controlled_buffer_8_out, INS[5:0]}), .data(rom_2_data));  // open: sel
  or or_3 (or_3_out, TS2, TS3, TS4, TS5);
  Pull_Resistor pull_resistor_2 (.node({L_W, Z_C, O, C_C, R_W, L_R, R_a, P, P_R, T_R, T_W, B_R, B_W, A_R, A_W, R_R}));
  assign {L_W, Z_C, O, C_C, R_W, L_R, R_a, P, P_R, T_R, T_W, B_R, B_W, A_R, A_W, R_R} = or_3_out ? rom_2_data : 16'bz;  // Controlled_Buffer controlled_buffer_12
  assign {L_W, Z_C, O, C_C, R_W, L_R, R_a, P, P_R, T_R, T_W, B_R, B_W, A_R, A_W, R_R} = I_R ? 16'h800 : 16'bz;  // Controlled_Buffer controlled_buffer_13
  assign {L_W, Z_C, O, C_C, R_W, L_R, R_a, P, P_R, T_R, T_W, B_R, B_W, A_R, A_W, R_R} = TS1 ? 16'h100 : 16'bz;  // Controlled_Buffer controlled_buffer_14

  // Other names for the same wires on the sheet: TS0 = I_R

  // Notes on the sheet:
  //   contents of rom_1 (hex, n*v repeats v):
  //   1 0 3 0 5 80 6 81 2 80 7 1 5 80 e a b 24 1 0 5 80 2 81 7 1 5 81 e a b 24 1 0 5 81 2 81 4 81 8 5 82 4
  //   82 8 5 82 4 82 8 5 82 4 82 8 4 80 8 5 c0 9 8
  //   contents of rom_2 (hex, n*v repeats v):
  //   0 804 840 910 4*840 48 6*840 48 49*0 100 b24 0 b30 323 329 522 422 a0 5*100 2422 55*0 8004 8004 0
  //   1020 3020 4020 6020 2422
endmodule

module ALU (
  input  CLOCK,
  input  WRITE,
  input  READ,
  input  OP,
  input  [7:0] IN1,
  input  [7:0] IN2,
  output [7:0] RES,
  output CARRY,
  output ZERO
);

  wire adder_1_cout, and_1_out, nor_1_out, not_1_out, not_2_out;
  wire [7:0] adder_1_out, controlled_buffer_1_out, negator_1_out, reg8_2_out, reg8_3_out;

  // Probe on reg8_2_out
  // Probe on controlled_buffer_1_out
  // Probe on adder_1_out
  reg8 reg8_1 (.OUT(RES), .CLOCK(not_1_out), .WRITE(WRITE), .READ(READ), .IN(adder_1_out));  // open: RST
  not not_1 (not_1_out, CLOCK);
  Adder adder_1 (.a(reg8_2_out), .b(controlled_buffer_1_out), .out(adder_1_out), .cout(adder_1_cout));  // open: cin
  nor nor_1 (nor_1_out, adder_1_out[7], adder_1_out[6], adder_1_out[5], adder_1_out[4], adder_1_out[3], adder_1_out[2], adder_1_out[1], adder_1_out[0]);
  and and_1 (and_1_out, CLOCK, READ);
  assign controlled_buffer_1_out = OP ? negator_1_out : 8'bz;  // Controlled_Buffer controlled_buffer_1
  not not_2 (not_2_out, OP);
  assign controlled_buffer_1_out = not_2_out ? reg8_3_out : 8'bz;  // Controlled_Buffer controlled_buffer_2
  D_Flip_Flop #(.trigger("falling")) d_ff_1 (
    .clk(and_1_out), .D(adder_1_cout), .Q(CARRY));  // open: Qn, preset, en, reset
  Pull_Resistor pull_resistor_1 (.node(WRITE));
  Pull_Resistor pull_resistor_2 (.node(OP));
  Negator negator_1 (.in(reg8_3_out), .out(negator_1_out));
  // Probe on negator_1_out
  D_Flip_Flop d_ff_2 (.clk(READ), .D(nor_1_out), .Q(ZERO), .en(READ));  // open: Qn, preset, reset
  Pull_Resistor pull_resistor_3 (.node(READ));
  reg8 reg8_2 (.OUT(reg8_2_out), .CLOCK(CLOCK), .WRITE(1'b1), .READ(READ), .IN(IN1));  // open: RST
  reg8 reg8_3 (.OUT(reg8_3_out), .CLOCK(CLOCK), .WRITE(1'b1), .READ(READ), .IN(IN2));  // open: RST
endmodule

module reg8 (
  input  RST,
  input  CLOCK,
  input  WRITE,
  input  READ,
  input  [7:0] IN,
  output [7:0] OUT
);

  wire controlled_buffer_9_out, d_ff_1_q, d_ff_2_q, d_ff_3_q, d_ff_4_q, d_ff_5_q, d_ff_6_q, d_ff_7_q,
       d_ff_8_q;

  assign OUT[0] = WRITE ? d_ff_1_q : 1'bz;  // Controlled_Buffer controlled_buffer_1
  D_Flip_Flop d_ff_1 (.clk(controlled_buffer_9_out), .D(IN[0]), .Q(d_ff_1_q), .reset(RST));  // open: Qn, preset, en
  assign OUT[1] = WRITE ? d_ff_2_q : 1'bz;  // Controlled_Buffer controlled_buffer_2
  D_Flip_Flop d_ff_2 (.clk(controlled_buffer_9_out), .D(IN[1]), .Q(d_ff_2_q), .reset(RST));  // open: Qn, preset, en
  assign OUT[2] = WRITE ? d_ff_3_q : 1'bz;  // Controlled_Buffer controlled_buffer_3
  D_Flip_Flop d_ff_3 (.clk(controlled_buffer_9_out), .D(IN[2]), .Q(d_ff_3_q), .reset(RST));  // open: Qn, preset, en
  assign OUT[3] = WRITE ? d_ff_4_q : 1'bz;  // Controlled_Buffer controlled_buffer_4
  D_Flip_Flop d_ff_4 (.clk(controlled_buffer_9_out), .D(IN[3]), .Q(d_ff_4_q), .reset(RST));  // open: Qn, preset, en
  assign OUT[4] = WRITE ? d_ff_5_q : 1'bz;  // Controlled_Buffer controlled_buffer_5
  D_Flip_Flop d_ff_5 (.clk(controlled_buffer_9_out), .D(IN[4]), .Q(d_ff_5_q), .reset(RST));  // open: Qn, preset, en
  assign OUT[5] = WRITE ? d_ff_6_q : 1'bz;  // Controlled_Buffer controlled_buffer_6
  D_Flip_Flop d_ff_6 (.clk(controlled_buffer_9_out), .D(IN[5]), .Q(d_ff_6_q), .reset(RST));  // open: Qn, preset, en
  assign OUT[6] = WRITE ? d_ff_7_q : 1'bz;  // Controlled_Buffer controlled_buffer_7
  D_Flip_Flop d_ff_7 (.clk(controlled_buffer_9_out), .D(IN[6]), .Q(d_ff_7_q), .reset(RST));  // open: Qn, preset, en
  assign OUT[7] = WRITE ? d_ff_8_q : 1'bz;  // Controlled_Buffer controlled_buffer_8
  D_Flip_Flop d_ff_8 (.clk(controlled_buffer_9_out), .D(IN[7]), .Q(d_ff_8_q), .reset(RST));  // open: Qn, preset, en
  assign controlled_buffer_9_out = READ ? CLOCK : 1'bz;  // Controlled_Buffer controlled_buffer_9
endmodule

module counter8 (
  input  RST,
  input  CLOCK,
  input  WRITE,
  input  READ,
  input  in_5,
  input  [7:0] IN,
  output [7:0] OUT
);

  wire and_1_out, and_2_out, and_3_out, and_4_out, and_5_out, and_6_out, and_7_out, and_8_out, and_9_out,
       and_10_out, and_11_out, and_12_out, and_13_out, and_14_out, and_15_out, and_16_out, d_ff_1_qn,
       d_ff_2_qn, d_ff_3_qn, d_ff_4_qn, d_ff_5_qn, d_ff_6_qn, d_ff_7_qn, d_ff_8_qn, not_1_out, or_1_out,
       or_2_out, or_3_out, or_4_out, or_5_out, or_6_out, or_7_out, or_8_out, undriven;
  wire [7:0] controlled_buffer_2_out, d_ff_1_q;

  assign OUT = WRITE ? d_ff_1_q : 8'bz;  // Controlled_Buffer controlled_buffer_1
  and and_1 (and_1_out, CLOCK, not_1_out, in_5);
  or or_1 (or_1_out, and_1_out, and_2_out);
  and and_2 (and_2_out, READ, CLOCK);
  D_Flip_Flop d_ff_1 (
    .clk(or_1_out), .D(controlled_buffer_2_out[0]), .Q(d_ff_1_q[0]), .Qn(d_ff_1_qn), .en(undriven),
    .reset(RST));  // open: preset
  assign controlled_buffer_2_out[0] = not_1_out ? d_ff_1_qn : 1'bz;  // Controlled_Buffer controlled_buffer_2
  or or_2 (or_2_out, and_4_out, and_3_out);
  and and_3 (and_3_out, READ, CLOCK);
  and and_4 (and_4_out, d_ff_1_qn, not_1_out);
  assign controlled_buffer_2_out[1] = not_1_out ? d_ff_2_qn : 1'bz;  // Controlled_Buffer controlled_buffer_3
  not not_1 (not_1_out, READ);
  D_Flip_Flop d_ff_2 (
    .clk(or_2_out), .D(controlled_buffer_2_out[1]), .Q(d_ff_1_q[1]), .Qn(d_ff_2_qn), .en(undriven),
    .reset(RST));  // open: preset
  and and_5 (and_5_out, d_ff_2_qn, not_1_out);
  or or_3 (or_3_out, and_5_out, and_6_out);
  and and_6 (and_6_out, READ, CLOCK);
  assign controlled_buffer_2_out[2] = not_1_out ? d_ff_3_qn : 1'bz;  // Controlled_Buffer controlled_buffer_4
  and and_7 (and_7_out, READ, CLOCK);
  D_Flip_Flop d_ff_3 (
    .clk(or_3_out), .D(controlled_buffer_2_out[2]), .Q(d_ff_1_q[2]), .Qn(d_ff_3_qn), .en(undriven),
    .reset(RST));  // open: preset
  and and_8 (and_8_out, d_ff_3_qn, not_1_out);
  or or_4 (or_4_out, and_8_out, and_7_out);
  D_Flip_Flop d_ff_4 (
    .clk(or_4_out), .D(controlled_buffer_2_out[3]), .Q(d_ff_1_q[3]), .Qn(d_ff_4_qn), .en(undriven),
    .reset(RST));  // open: preset
  assign controlled_buffer_2_out[3] = not_1_out ? d_ff_4_qn : 1'bz;  // Controlled_Buffer controlled_buffer_5
  or or_5 (or_5_out, and_10_out, and_9_out);
  and and_9 (and_9_out, READ, CLOCK);
  and and_10 (and_10_out, d_ff_4_qn, not_1_out);
  assign controlled_buffer_2_out[4] = not_1_out ? d_ff_5_qn : 1'bz;  // Controlled_Buffer controlled_buffer_6
  D_Flip_Flop d_ff_5 (
    .clk(or_5_out), .D(controlled_buffer_2_out[4]), .Q(d_ff_1_q[4]), .Qn(d_ff_5_qn), .en(undriven),
    .reset(RST));  // open: preset
  and and_11 (and_11_out, d_ff_5_qn, not_1_out);
  or or_6 (or_6_out, and_11_out, and_12_out);
  and and_12 (and_12_out, READ, CLOCK);
  D_Flip_Flop d_ff_6 (
    .clk(or_6_out), .D(controlled_buffer_2_out[5]), .Q(d_ff_1_q[5]), .Qn(d_ff_6_qn), .en(undriven),
    .reset(RST));  // open: preset
  assign controlled_buffer_2_out[5] = not_1_out ? d_ff_6_qn : 1'bz;  // Controlled_Buffer controlled_buffer_7
  and and_13 (and_13_out, READ, CLOCK);
  and and_14 (and_14_out, d_ff_6_qn, not_1_out);
  or or_7 (or_7_out, and_14_out, and_13_out);
  D_Flip_Flop d_ff_7 (
    .clk(or_7_out), .D(controlled_buffer_2_out[6]), .Q(d_ff_1_q[6]), .Qn(d_ff_7_qn), .en(undriven),
    .reset(RST));  // open: preset
  assign controlled_buffer_2_out[6] = not_1_out ? d_ff_7_qn : 1'bz;  // Controlled_Buffer controlled_buffer_8
  assign controlled_buffer_2_out = READ ? IN : 8'bz;  // Controlled_Buffer controlled_buffer_9
  or or_8 (or_8_out, and_16_out, and_15_out);
  and and_15 (and_15_out, READ, CLOCK);
  and and_16 (and_16_out, d_ff_7_qn, not_1_out);
  assign controlled_buffer_2_out[7] = not_1_out ? d_ff_8_qn : 1'bz;  // Controlled_Buffer controlled_buffer_10
  D_Flip_Flop d_ff_8 (
    .clk(or_8_out), .D(controlled_buffer_2_out[7]), .Q(d_ff_1_q[7]), .Qn(d_ff_8_qn), .en(undriven),
    .reset(RST));  // open: preset
endmodule
